// Logisim project micro.circ as structural Verilog: 11 circuits, main circuit Main Board
module Main_Board (
  output Stop
);

  wire CLK, isabel_1_ram_chip_select, isabel_1_ram_read, isabel_1_ram_write, RESET;
  wire [7:0] isabel_1_ram_addr, isabel_1_ram_data_in, isabel_1_rom_addr, ram_1_data;
  wire [15:0] ram_2_data;

  Button button_1 (.out(RESET));
  Clock clock_1 (.out(CLK));
  RAM #(.bus("separate")) ram_1 (
    .addr(isabel_1_ram_addr), .din(isabel_1_ram_data_in), .data(ram_1_data), .str(isabel_1_ram_write),
    .sel(isabel_1_ram_chip_select), .clk(CLK), .ld(isabel_1_ram_read), .clr(RESET));
  ISABEL isabel_1 (
    .ROM_Data(ram_2_data), .ROM_Addr(isabel_1_rom_addr), .RAM_Addr(isabel_1_ram_addr),
    .RAM_Data_In(isabel_1_ram_data_in), .RAM_Data_Out(ram_1_data),
    .RAM_Chip_Select(isabel_1_ram_chip_select), .RAM_Read(isabel_1_ram_read), .Clock(CLK), .Reset(RESET),
    .Stop(Stop), .RAM_Write(isabel_1_ram_write));
  RAM #(.dataWidth(16), .bus("asynch")) ram_2 (
    .addr(isabel_1_rom_addr), .data(ram_2_data), .sel(1'b1), .ld(1'b1), .clr(1'b0));

  // Notes on the sheet:
  //   RAM
  //   ROM
endmodule

module ISABEL (
  input  Clock,
  input  Reset,
  input  [15:0] ROM_Data,
  input  [7:0] RAM_Data_Out,
  output [7:0] RAM_Addr,
  output [7:0] ROM_Addr,
  output [7:0] RAM_Data_In,
  output Stop,
  output RAM_Chip_Select,
  output RAM_Read,
  output RAM_Write
);

  wire alu_1_out_5, alu_1_out_6, EN, EnZN, JMP, JN, JR, JZ, N, Z;
  wire [1:0] Origen;
  wire [2:0] AA, AB, AB_a, DA, Op;
  wire [7:0] ALU, B, branch_control_unit_1_out_10, K, multiplexer_1_out;

  Inst_Decoder inst_decoder_1 (
    .in_1(ROM_Data), .out_2(DA), .out_4(AB), .out_6(K), .out_15(Op), .out_16(Origen), .out_3(RAM_Write),
    .out_5(EN), .out_7(EnZN), .out_9(JMP), .out_10(JZ), .out_12(JN), .out_13(JR), .out_14(AA),
    .out_8(RAM_Read), .Stop(Stop));
  Multiplexer #(.select(2), .width(8), .enable("false")) multiplexer_1 (
    .in0(K), .in1(RAM_Data_Out), .in2(RAM_Data_In), .in3(ALU), .out(multiplexer_1_out), .sel(Origen));
  Registers registers_1 (
    .in_1(DA), .in_3(AA), .in_4(EN), .in_5(AB_a), .in_6(multiplexer_1_out), .out_7(RAM_Data_In), .out_8(B),
    .in_2(Clock));
  Branch_Control_Unit branch_control_unit_1 (
    .in_1(JMP), .in_2(JN), .in_3(JZ), .in_4(N), .in_5(Z), .in_6(JR), .in_7(K), .in_8(RAM_Data_In),
    .in_9(ROM_Addr), .out_10(branch_control_unit_1_out_10));
  or or_1 (RAM_Chip_Select, RAM_Read, RAM_Write);
  Multiplexer #(.width(8), .enable("false")) multiplexer_2 (.in0(B), .in1(RAM_Data_In), .out(RAM_Addr), .sel(RAM_Read));
  ALU alu_1 (.in_2(RAM_Data_In), .in_3(B), .in_1(Op), .out_4(ALU), .out_5(alu_1_out_5), .out_6(alu_1_out_6));
  Register PC (.D(branch_control_unit_1_out_10), .Q(ROM_Addr), .clk(Clock), .clr(Reset));  // open: en
  Multiplexer #(.width(3), .enable("false")) multiplexer_3 (.in0(AB), .in1(DA), .out(AB_a), .sel(RAM_Write));
  D_Flip_Flop d_ff_1 (.clk(Clock), .D(alu_1_out_5), .Q(Z), .en(EnZN));  // open: Qn, preset, reset
  D_Flip_Flop d_ff_2 (.clk(Clock), .D(alu_1_out_6), .Q(N), .en(EnZN));  // open: Qn, preset, reset

  // Other names for the same wires on the sheet: CLK = Clock; RAM_A[7:0] = RAM_Addr; RAM_CS = RAM_Chip_Select;
  //   A[7:0] = RAM_Data_In; RAM_DIn[7:0] = RAM_Data_In; RAM_DOut[7:0] = RAM_Data_Out; RAM_R = RAM_Read;
  //   RAM_W = RAM_Write; ROM_A[7:0] = ROM_Addr; ROM_D[15:0] = ROM_Data; RST = Reset

  // Notes on the sheet:
  //   ROM Interface
  //   RAM Interface
  //   Control
endmodule

module Registers (
  input  [2:0] in_1,
  input  in_2,
  input  [2:0] in_3,
  input  in_4,
  input  [2:0] in_5,
  input  [7:0] in_6,
  output [7:0] out_7,
  output [7:0] out_8
);

  wire demultiplexer_1_out0, demultiplexer_1_out1, demultiplexer_1_out2, demultiplexer_1_out3,
       demultiplexer_1_out4, demultiplexer_1_out5, demultiplexer_1_out6, demultiplexer_1_out7;
  wire [7:0] R0, R1, R2, R3, R4, R5, R6, R7;

  Demultiplexer #(.select(3), .enable("false")) demultiplexer_1 (
    .out0(demultiplexer_1_out0), .out1(demultiplexer_1_out1), .out2(demultiplexer_1_out2),
    .out3(demultiplexer_1_out3), .out4(demultiplexer_1_out4), .out5(demultiplexer_1_out5),
    .out6(demultiplexer_1_out6), .out7(demultiplexer_1_out7), .in(in_4), .sel(in_1));
  Register register_1 (.D(in_6), .en(demultiplexer_1_out0), .Q(R0), .clk(in_2));  // open: clr
  Register register_2 (.D(in_6), .en(demultiplexer_1_out1), .Q(R1), .clk(in_2));  // open: clr
  Register register_3 (.D(in_6), .en(demultiplexer_1_out2), .Q(R2), .clk(in_2));  // open: clr
  Register register_4 (.D(in_6), .en(demultiplexer_1_out3), .Q(R3), .clk(in_2));  // open: clr
  Register register_5 (.D(in_6), .en(demultiplexer_1_out4), .Q(R4), .clk(in_2));  // open: clr
  Register register_6 (.D(in_6), .en(demultiplexer_1_out5), .Q(R5), .clk(in_2));  // open: clr
  Register register_7 (.D(in_6), .en(demultiplexer_1_out6), .Q(R6), .clk(in_2));  // open: clr
  Register register_8 (.D(in_6), .en(demultiplexer_1_out7), .Q(R7), .clk(in_2));  // open: clr
  Multiplexer #(.select(3), .width(8), .enable("false")) multiplexer_1 (
    .in0(R0), .in1(R1), .in2(R2), .in3(R3), .in4(R4), .in5(R5), .in6(R6), .in7(R7), .out(out_7), .sel(in_3));
  Multiplexer #(.select(3), .width(8), .enable("false")) multiplexer_2 (
    .in0(R0), .in1(R1), .in2(R2), .in3(R3), .in4(R4), .in5(R5), .in6(R6), .in7(R7), .out(out_8), .sel(in_5));

  // Other names for the same wires on the sheet: AA[2:0] = in_3; AB[2:0] = in_5; CLK = in_2; DA[2:0] = in_1
endmodule

module ALU (
  input  [2:0] in_1,
  input  [7:0] in_2,
  input  [7:0] in_3,
  output [7:0] out_4,
  output out_5,
  output out_6
);

  wire [7:0] adder_1_out, and_1_out_3, multiplier_1_out, not_1_out_2, or_1_out_3, subtractor_1_out, undriven,
       xor_1_out_3;

  Adder adder_1 (.a(in_2), .b(in_3), .out(adder_1_out));  // open: cin, cout
  Subtractor subtractor_1 (.a(in_2), .b(in_3), .out(subtractor_1_out));  // open: bin, bout
  Multiplier multiplier_1 (.a(in_2), .b(in_3), .out(multiplier_1_out));  // open: cin, cout
  Negator negator_1 (.in(in_2));  // open: out
  AND and_1 (.in_1(in_2), .in_2(in_3), .out_3(and_1_out_3));
  OR or_1 (.in_1(in_2), .in_2(in_3), .out_3(or_1_out_3));
  XOR xor_1 (.in_1(in_2), .in_2(in_3), .out_3(xor_1_out_3));
  NOT not_1 (.in_1(in_2), .out_2(not_1_out_2));
  Multiplexer #(.select(3), .width(8), .enable("false")) multiplexer_1 (
    .in0(adder_1_out), .in1(subtractor_1_out), .in2(multiplier_1_out), .in3(undriven), .in4(and_1_out_3),
    .in5(or_1_out_3), .in6(xor_1_out_3), .in7(not_1_out_2), .out(out_4), .sel(in_1));
  or or_2 (out_5, out_4[0], out_4[1], out_4[2], out_4[3], out_4[4], out_4[5], out_4[6], out_4[7]);

  assign out_6 = out_4[7];

  // Other names for the same wires on the sheet: OP[2:0] = in_1
endmodule

module NOT (
  input  [7:0] in_1,
  output [7:0] out_2
);

  not not_1 (out_2[0], in_1[0]);
  not not_2 (out_2[1], in_1[1]);
  not not_3 (out_2[2], in_1[2]);
  not not_4 (out_2[3], in_1[3]);
  not not_5 (out_2[4], in_1[4]);
  not not_6 (out_2[5], in_1[5]);
  not not_7 (out_2[6], in_1[6]);
  not not_8 (out_2[7], in_1[7]);
endmodule

module AND (
  input  [7:0] in_1,
  input  [7:0] in_2,
  output [7:0] out_3
);

  assign out_3 = in_1 & in_2;  // AND_Gate and_1, 8 bits wide
endmodule

module OR (
  input  [7:0] in_1,
  input  [7:0] in_2,
  output [7:0] out_3
);

  assign out_3 = in_1 | in_2;  // OR_Gate or_1, 8 bits wide
endmodule

module XOR (
  input  [7:0] in_1,
  input  [7:0] in_2,
  output [7:0] out_3
);

  assign out_3 = in_1 ^ in_2;  // XOR_Gate xor_1, 8 bits wide
endmodule

module Inst_Decoder (
  input  [15:0] in_1,
  output [2:0] out_2,
  output out_3,
  output [2:0] out_4,
  output out_5,
  output [7:0] out_6,
  output out_7,
  output out_8,
  output out_9,
  output out_10,
  output Stop,
  output out_12,
  output out_13,
  output [2:0] out_14,
  output [2:0] out_15,
  output [1:0] out_16
);

  wire decoder_1_out4, decoder_1_out5, decoder_1_out6, decoder_1_out7, decoder_1_out8, decoder_1_out9,
       decoder_1_out10, decoder_1_out11, EnR_MK, EnR_MRR, Jump, or_4_out, reading_1_k_nor;
  wire [2:0] RB;
  wire [3:0] OpCode;

  Decoder #(.select(4), .enable("false")) decoder_1 (
    .out0(EnR_MK), .out1(EnR_MRR), .out2(out_8), .out3(out_3), .out4(decoder_1_out4), .out5(decoder_1_out5),
    .out6(decoder_1_out6), .out7(decoder_1_out7), .out8(decoder_1_out8), .out9(decoder_1_out9),
    .out10(decoder_1_out10), .out11(decoder_1_out11), .out12(Jump), .out13(out_10), .out14(out_12),
    .out15(out_13), .sel(OpCode));
  Reading reading_1 (.in_1(in_1), .OpCode(OpCode), .RA(out_2), .RB(RB), .RC(out_4), .K(out_6), .K_NOR(reading_1_k_nor));
  Multiplexer #(.width(3), .enable("false")) multiplexer_1 (.in0(RB), .in1(out_2), .out(out_14), .sel(out_13));
  and and_1 (Stop, reading_1_k_nor, Jump);
  or or_1 (out_5, EnR_MRR, out_7, out_8, EnR_MK);
  or or_2 (out_9, Jump, out_13);
  or or_3 (out_7, decoder_1_out11, decoder_1_out10, decoder_1_out9, decoder_1_out8, decoder_1_out7, decoder_1_out6, decoder_1_out5, decoder_1_out4);
  Priority_Encoder #(.disabled(0)) priority_encoder_1 (
    .in0(decoder_1_out4), .in1(decoder_1_out5), .in2(decoder_1_out6), .in3(decoder_1_out7),
    .in4(decoder_1_out8), .in5(decoder_1_out9), .in6(decoder_1_out10), .in7(decoder_1_out11), .out(out_15),
    .en_in(out_7));  // open: gs, en_out
  or or_4 (or_4_out, out_7, EnR_MK, out_8, EnR_MRR);
  Priority_Encoder #(.select(2), .disabled(0)) priority_encoder_2 (
    .in0(EnR_MK), .in1(out_8), .in2(EnR_MRR), .in3(out_7), .out(out_16), .en_in(or_4_out));  // open: gs, en_out

  // Other names for the same wires on the sheet: EnR = out_5; EnR_ALU = out_7; EnZN = out_7; JMP = out_9; JN = out_12;
  //   JR = out_13; JZ = out_10; K[7:0] = out_6; RA[2:0] = out_2; En_Ram = out_8; RAM_R = out_8; RAM_W = out_3;
  //   RC[2:0] = out_4
endmodule

module Branch_Control_Unit (
  input  in_1,
  input  in_2,
  input  in_3,
  input  in_4,
  input  in_5,
  input  in_6,
  input  [7:0] in_7,
  input  [7:0] in_8,
  input  [7:0] in_9,
  output [7:0] out_10
);

  wire and_1_out, and_2_out, Jump;
  wire [7:0] A, adder_1_out, adder_2_out;

  and and_1 (and_1_out, in_2, in_4);
  and and_2 (and_2_out, in_3, in_5);
  or or_1 (Jump, in_1, and_1_out, and_2_out);
  Adder adder_1 (.a(in_9), .b(8'h1), .out(adder_1_out));  // open: cin, cout
  Adder adder_2 (.a(in_9), .b(A), .out(adder_2_out));  // open: cin, cout
  Multiplexer #(.width(8), .enable("false")) multiplexer_1 (
    .in0(adder_1_out), .in1(adder_2_out), .out(out_10), .sel(Jump));
  Multiplexer #(.width(8), .enable("false")) multiplexer_2 (.in0(in_7), .in1(in_8), .out(A), .sel(in_6));

  // Other names for the same wires on the sheet: JMP = in_1; JN = in_2; JR = in_6; JZ = in_3; K[7:0] = in_7; N = in_4;
  //   PC_in[7:0] = out_10; PC_out[7:0] = in_9; Reg[7:0] = in_8; Z = in_5
endmodule

module Reading (
  input  [15:0] in_1,
  output [3:0] OpCode,
  output [2:0] RA,
  output [2:0] RB,
  output [2:0] RC,
  output [7:0] K,
  output K_NOR
);

  nor nor_1 (K_NOR, in_1[7], in_1[6], in_1[5], in_1[4], in_1[3], in_1[2], in_1[1], in_1[0]);

  assign K = in_1[7:0];
  assign OpCode = in_1[15:12];
  assign RA = in_1[11:9];
  assign RB = in_1[8:6];
  assign RC = in_1[5:3];
endmodule
